# Fritzing sketch Quadcopter_6050 (saved by Fritzing 0.9.2b)
circuit board: 6.88566cm x 5.36311cm
breadboards: 1

parts:
  J1 = Basic Servo
  J2 = Basic Servo
  J3 = Basic Servo
  J4 = Basic Servo
  Hip_Cat_v1_0_0_1 = Arduino Uno (Rev3)
  GY2 = MPU-6050 Board GY-521 [form="♀ (female)" package=THT]
  S1 = Pushbutton [package="[THT]"]
  LED1 = LED - 5mm [color="Red (633nm)" package="5 mm [THT]"]
  R1 = Resistor [tolerance=±5% resistance=220 package=THT]
  J0 = female pin header, 2 pins [form="♀ (female)"]
  J5 = Basic Servo
  J6 = Basic Servo
  J7 = female pin header, 5 pins [form="♀ (female)"]
  J8 = female pin header, 5 pins [form="♀ (female)"]
  3v = female pin header, 2 pins [form="♀ (female)"]
  5v = female pin header, 2 pins [form="♀ (female)"]

nets:
  GND: J1.gnd, J2.gnd, J3.gnd, J4.gnd, Hip_Cat_v1_0_0_1.GND, GY2.pin2, S1.Pin_3, S1.Pin_4, R1.Pin_0, J5.gnd, J6.gnd, J7.pin1, J8.pin1, 3v.pin1, 5v.pin1
  N1: J1.pulse, Hip_Cat_v1_0_0_1.D6_PWM
  N2: J2.pulse, Hip_Cat_v1_0_0_1.D9_PWM
  N3: J3.pulse, Hip_Cat_v1_0_0_1.D10_PWM/SS
  N4: J4.vcc, J0.pin1
  N5: J4.pulse, Hip_Cat_v1_0_0_1.D11_PWM/MOSI
  N6: Hip_Cat_v1_0_0_1.A0, J8.pin2
  N7: Hip_Cat_v1_0_0_1.A1, J8.pin3
  N8: Hip_Cat_v1_0_0_1.A2, J8.pin4
  N9: Hip_Cat_v1_0_0_1.A3, J8.pin5
  N10: Hip_Cat_v1_0_0_1.A4/SDA, GY2.pin4
  N11: Hip_Cat_v1_0_0_1.A5/SCL, GY2.pin3
  N12: Hip_Cat_v1_0_0_1.D8, J7.pin3
  N13: Hip_Cat_v1_0_0_1.D12/MISO, J7.pin2
  N14: Hip_Cat_v1_0_0_1.D13/SCK, LED1.anode
  N15: Hip_Cat_v1_0_0_1.D2, GY2.pin8
  N16: Hip_Cat_v1_0_0_1.D3_PWM, J6.pulse
  N17: Hip_Cat_v1_0_0_1.D4, J7.pin5
  N18: Hip_Cat_v1_0_0_1.D5_PWM, J5.pulse
  N19: Hip_Cat_v1_0_0_1.D7, J7.pin4
  N20: Hip_Cat_v1_0_0_1.RESET, S1.Pin_1, S1.Pin_2
  N21: Hip_Cat_v1_0_0_1.3V3, GY2.pin1, 3v.pin2
  N22: Hip_Cat_v1_0_0_1.5V, 5v.pin2
  N23: Hip_Cat_v1_0_0_1.VIN, J0.pin2
  N24: LED1.cathode, R1.Pin_1

notes:
  Amir Aliabadi

custom parts:
  MPU-6050 Board GY-521: Acelerometro y Giroscopio MPU-6050 Board GY-521
